// Digital circuit cpu_pipeline.dig as structural Verilog
module cpu_pipeline (
  input  rst,
  input  clk,
  output [31:0] dmem_addr,
  output [31:0] dmem_wdata,
  output dmem_we,
  output [31:0] imem_addr,
  output dmem_re
);

  wire [31:0] ramdualport_1_d, rom_1_d;

  cpu_pipeline #(.applicationType("GHDL"), .CodeFile("/home/luiz-cavalini/AC-CPU-RV32I/digital/cpu_pipeline_full.vhd")) u_cpu_pipeline (
    .clk_i(clk), .rst_i(rst), .imem_data_i(rom_1_d), .dmem_rdata_i(ramdualport_1_d),
    .imem_addr_o({imem_addr[31:8], imem_addr[9:8], imem_addr[9:8], imem_addr[9:8], imem_addr[9:8]}),
    .dmem_addr_o({dmem_addr[31:8], dmem_addr[9:8], dmem_addr[9:8], dmem_addr[9:8], dmem_addr[9:8]}),
    .dmem_wdata_o(dmem_wdata), .dmem_we_o(dmem_we), .dmem_re_o(dmem_re));
  RAMDualPort #(.AddrBits(10), .Bits(32)) ramdualport_1 (
    .A({dmem_addr[9:8], dmem_addr[9:8], dmem_addr[9:8], dmem_addr[9:8], dmem_addr[9:8]}), .Din(dmem_wdata),
    .str(dmem_we), .C(clk), .ld(dmem_re), .D(ramdualport_1_d));
  ROM #(.AddrBits(24), .isProgramMemory("true"), .Bits(32)) rom_1 (
    .A({imem_addr[23:8], imem_addr[9:8], imem_addr[9:8], imem_addr[9:8], imem_addr[9:8]}), .sel(1'b1),
    .D(rom_1_d));
  // Pins of 8 and 10 and 32 bits meet at {dmem_addr[31:8], dmem_addr[9:8], dmem_addr[9:8], dmem_addr[9:8], dmem_addr[9:8]}
  // Pins of 8 and 24 and 32 bits meet at {imem_addr[31:8], imem_addr[9:8], imem_addr[9:8], imem_addr[9:8], imem_addr[9:8]}

  assign dmem_addr[7:0] = {dmem_addr[9:8], dmem_addr[9:8], dmem_addr[9:8], dmem_addr[9:8]};
  assign imem_addr[7:0] = {imem_addr[9:8], imem_addr[9:8], imem_addr[9:8], imem_addr[9:8]};
  // also tied to GND on the sheet: {imem_addr[8], imem_addr[10], imem_addr[13], imem_addr[15], imem_addr[16], imem_addr[17], imem_addr[18], imem_addr[19], imem_addr[20], imem_addr[21], imem_addr[22], imem_addr[23], imem_addr[24], imem_addr[25], imem_addr[26], imem_addr[27], imem_addr[28], imem_addr[29], imem_addr[30], imem_addr[31]}
  // also tied to VCC on the sheet: {imem_addr[9], imem_addr[11], imem_addr[12], imem_addr[14]}

  // Notes on the sheet:
  //   rom_1 loads program.hex
endmodule
